# Fritzing sketch badge-full (saved by Fritzing 0.9.3b)
circuit board: 10cm x 10cm
breadboards: 1

parts:
  ↑ = SWITCH-MOMENTARY-2 [package=tactile_switch_tall]
  → = SWITCH-MOMENTARY-2 [package=tactile_switch_tall]
  ← = SWITCH-MOMENTARY-2 [package=tactile_switch_tall]
  ↓ = SWITCH-MOMENTARY-2 [package=tactile_switch_tall]
  s = SWITCH-MOMENTARY-2 [package=tactile_switch_tall]
  z = SWITCH-MOMENTARY-2 [package=tactile_switch_tall]
  o = SWITCH-MOMENTARY-2 [package=tactile_switch_tall]
  x = SWITCH-MOMENTARY-2 [package=tactile_switch_tall]
  X4 = mystery part, 11 pins [chip_label=?]
  X5 = mystery part, 11 pins [chip_label=?]
  U3 = mystery part, 11 pins [chip_label=?]
  U4 = mystery part, 11 pins [chip_label=?]
  +_- = Battery
  R1 = Resistor [tolerance=±5% resistance=20k package="0603 [SMD]"]
  R2 = Resistor [tolerance=±5% resistance=100k package="0603 [SMD]"]
  R3 = Resistor [tolerance=±5% resistance=100k package="0603 [SMD]"]
  R4 = Resistor [tolerance=±5% resistance=4.7k package="0603 [SMD]"]
  R5 = Resistor [tolerance=±5% resistance=4.7k package="0603 [SMD]"]
  C1 = Ceramic Capacitor [capacitance=1µF package="0603 [SMD, multilayer]"]
  X2 = SPST Switch [package=switch-spst-smd-a]
  X1 = USB Connectors [package=usb-microb]
  U1 = TQFP32 [chip_label=IC package=TQFP]
  U3_2 = Voltage Regulator LDO [package=sot23-5]
  C3 = Ceramic Capacitor [capacitance=1µF package="0603 [SMD, multilayer]"]
  C2 = Ceramic Capacitor [capacitance=1µF package="0603 [SMD, multilayer]"]
  U4_2 = AT25FS010 [package=so08wide]
  R6 = Resistor [tolerance=±5% resistance=4.7k package="0603 [SMD]"]
  C4 = Ceramic Capacitor [capacitance=1µF package="0603 [SMD, multilayer]"]
  U1_2 = QFN-32 [chip_label=IC package=QFN]
  GND_3V3_A0 = female pin header, 4 pins [form="♀ (female)"]
  GND_3V3_SDA_SCL = female pin header, 4 pins [form="♀ (female)"]
  X3 = female pin header, 8 pins [form="♀ (female)"]
  C5 = Ceramic Capacitor [capacitance=1µF package="0603 [SMD, multilayer]"]
  U5 = LGA-16 [chip_label=IC package=QFN]
  U2 = QFN-48 [chip_label=IC package=QFN]

nets:
  button UP: ↑.2, U1.PA27, U1_2.25
  GND: ↑.1, →.1, ←.1, ↓.1, s.2, z.2, o.2, x.2, +_-.-, R1.Pin_0, R3.Pin_0, C1.1, X1.GND, U1.GND, U3_2.GND, C3.1, C2.1, U4_2.GND, C4.0, U1_2.10, U1_2.28, GND_3V3_A0.pin1, GND_3V3_SDA_SCL.pin1, X3.pin7, C5.0, U5.GND, U5.SDO/SA0, U5.RES, U2.5, U2.12, U2.34, U2.43, U2.44, U2.48, U2.thermal
  button RIGHT: →.2, U1.PA22, U1_2.21
  button LEFT: ←.2, U1.PA28, U1_2.27
  button DOWN: ↓.2, U1.PA23, U1_2.22
  button S: s.1, U1.PA15, U1_2.16
  button Z: z.1, U1.PA10, U1_2.13
  button O: o.1, U1.PA14, U1_2.15
  button X: x.1, U1.PA11, U1_2.14
  COL9: X4.pin2, X5.pin2, U2.7
  R3B: X4.pin3, U2.31
  R1B: X4.pin4, U2.32
  COL7: X4.pin5, X5.pin5, U2.6
  COL4: X4.pin8, X5.pin8, U2.4
  R2B: X4.pin9, U2.33
  COL2: X4.pin10, X5.pin10, U2.3
  COL1: X4.pin11, X5.pin11, U2.2
  R3A: X5.pin3, U2.21
  R1A: X5.pin4, U2.22
  R2A: X5.pin9, U2.23
  COL3: U3.pin2, U4.pin2, U2.14
  R5A: U3.pin3, U2.16
  R7A: U3.pin4, U2.17
  COL5: U3.pin5, U4.pin5, U2.13
  COL6: U3.pin6, U4.pin6, U2.11
  R4A: U3.pin7, U2.18
  COL8: U3.pin8, U4.pin8, U2.10
  R6A: U3.pin9, U2.19
  COL10: U3.pin10, U4.pin10, U2.9
  COL11: U3.pin11, U4.pin11, U2.8
  R5B: U4.pin3, U2.26
  R7B: U4.pin4, U2.27
  R4B: U4.pin7, U2.28
  R6B: U4.pin9, U2.30
  N1: +_-.+, X2.O
  N2: R1.Pin_1, U2.35
  3.3V: R2.Pin_0, R4.Pin_0, R5.Pin_0, C1.0, U1.VDDANA, U1.VDDIN, U3_2.OUT, C3.0, U4_2.WP, U4_2.HOLD, U4_2.VCC, R6.Pin_0, U1_2.9, U1_2.30, GND_3V3_A0.pin2, GND_3V3_SDA_SCL.pin2, X3.pin8, C5.1, U5.VDD_IO, U5.CS, U5.VDD, U2.39
  N3: R2.Pin_1, U2.46
  N4: R3.Pin_1, U2.47
  SCL0: R4.Pin_1, U1.PA09, U1_2.12, U5.SCL/SPC, U2.42
  SDA0: R5.Pin_1, U1.PA08, U1_2.11, U5.SDA/SDI/SDO, U2.41
  5V: X2.P, U3_2.IN, U3_2.EN, C4.1, U2.20, U2.29, U2.37, U2.38
  N5: X2.S, X1.VBUS
  D+: X1.D+, U1.PA25, U1_2.24
  D-: X1.D-, U1.PA24, U1_2.23
  SDA: U1.PA00, U1_2.1, GND_3V3_SDA_SCL.pin3
  SCL: U1.PA01, U1_2.2, GND_3V3_SDA_SCL.pin4
  A0: U1.PA02, U1_2.3, GND_3V3_A0.pin3
  radio0: U1.PA03, U1_2.4, X3.pin6
  radio1: U1.PA04, U1_2.5, X3.pin5
  radio2: U1.PA05, U1_2.6, X3.pin4
  radio3: U1.PA06, U1_2.7, X3.pin3
  radio4: U1.PA07, U1_2.8, X3.pin2
  flash MOSI: U1.PA16, U4_2.SI, U1_2.17
  flash SCK: U1.PA17, U4_2.SCK, U1_2.18
  flash CS: U1.PA18, U4_2.CS, R6.Pin_1, U1_2.19
  flash MISO: U1.PA19, U4_2.SO, U1_2.20
  reset: U1.!RESET, U1_2.26
  1.8V: U1.VDDCORE, C2.0, U1_2.29
  SWD: U1.PA30, U1_2.31
  SWC: U1.PA31, U1_2.32

notes:
  R
  C
  D
  CircuitPython Badge, A conference badge running CircuitPython. For details see https://hackaday.io/project/100853, 1.0
